// Logisim project control-logic.circ as structural Verilog: 1 circuit, main circuit control_logic
module control_logic (
  input  [31:0] Instruction,
  input  BrEq,
  input  BrLt,
  output PCSel,
  output RegWEn,
  output [2:0] ImmSel,
  output BrUn,
  output ASel,
  output BSel,
  output [3:0] ALUSel,
  output MemWEn,
  output [1:0] WBSel
);

  wire and_2_out, and_5_out, and_6_out, comparator_2_eq, comparator_3_eq, comparator_4_eq, comparator_5_eq,
       comparator_6_eq, comparator_7_eq, comparator_8_eq, comparator_9_eq, comparator_10_eq,
       comparator_11_eq, comparator_12_eq, Is_addi, Is_andi, Is_I_Imm, Is_ori, Is_slli, Is_slti, Is_srai,
       Is_srli, Is_xori;
  wire [5:0] INPUT_ROM;
  wire [15:14] rom_1_data;

  Comparator #(.mode("unsigned"), .width(7)) comparator_1 (
    .a(7'b0010011), .b(Instruction[6:0]), .eq(Is_I_Imm));  // open: gt, lt
  Comparator #(.mode("unsigned"), .width(3)) comparator_2 (
    .a(Instruction[14:12]), .b(3'b000), .eq(comparator_2_eq));  // open: gt, lt
  Comparator #(.mode("unsigned"), .width(3)) comparator_3 (
    .a(Instruction[14:12]), .b(3'b001), .eq(comparator_3_eq));  // open: gt, lt
  Comparator #(.mode("unsigned"), .width(3)) comparator_4 (
    .a(Instruction[14:12]), .b(3'b010), .eq(comparator_4_eq));  // open: gt, lt
  Comparator #(.mode("unsigned"), .width(3)) comparator_5 (
    .a(Instruction[14:12]), .b(3'b100), .eq(comparator_5_eq));  // open: gt, lt
  Comparator #(.mode("unsigned"), .width(3)) comparator_6 (
    .a(Instruction[14:12]), .b(3'b101), .eq(comparator_6_eq));  // open: gt, lt
  Comparator #(.mode("unsigned"), .width(3)) comparator_7 (
    .a(Instruction[14:12]), .b(3'b101), .eq(comparator_7_eq));  // open: gt, lt
  Comparator #(.mode("unsigned"), .width(3)) comparator_8 (
    .a(Instruction[14:12]), .b(3'b110), .eq(comparator_8_eq));  // open: gt, lt
  Comparator #(.mode("unsigned"), .width(3)) comparator_9 (
    .a(Instruction[14:12]), .b(3'b111), .eq(comparator_9_eq));  // open: gt, lt
  and and_1 (Is_addi, comparator_2_eq, Is_I_Imm);
  and and_2 (and_2_out, comparator_3_eq, Is_I_Imm);
  Comparator #(.mode("unsigned"), .width(7)) comparator_10 (
    .a(Instruction[31:25]), .b({7{1'b0}}), .eq(comparator_10_eq));  // open: gt, lt
  and and_3 (Is_slti, comparator_4_eq, Is_I_Imm);
  and and_4 (Is_xori, comparator_5_eq, Is_I_Imm);
  and and_5 (and_5_out, comparator_6_eq, Is_I_Imm);
  Comparator #(.mode("unsigned"), .width(7)) comparator_11 (
    .a(Instruction[31:25]), .b({7{1'b0}}), .eq(comparator_11_eq));  // open: gt, lt
  and and_6 (and_6_out, comparator_7_eq, Is_I_Imm);
  Comparator #(.mode("unsigned"), .width(7)) comparator_12 (
    .a(Instruction[31:25]), .b(7'b0100000), .eq(comparator_12_eq));  // open: gt, lt
  and and_7 (Is_ori, comparator_8_eq, Is_I_Imm);
  and and_8 (Is_andi, comparator_9_eq, Is_I_Imm);
  and and_9 (Is_slli, and_2_out, comparator_10_eq);
  and and_10 (Is_srli, and_5_out, comparator_11_eq);
  and and_11 (Is_srai, and_6_out, comparator_12_eq);
  ROM #(.addrWidth(6), .dataWidth(16)) rom_1 (
    .addr(INPUT_ROM), .data({rom_1_data, WBSel, MemWEn, ALUSel, BSel, ASel, BrUn, ImmSel, RegWEn}));
  Priority_Encoder #(.select_enc(6)) priority_encoder_1 (
    .in15(Is_addi), .in16(Is_slli), .in17(Is_slti), .in18(Is_xori), .in19(Is_srli), .in20(Is_srai),
    .in21(Is_ori), .in22(Is_andi), .out(INPUT_ROM));  // open: in0, in1, in2, in3, in4, in5, in6, in7, in8, in9, in10, in11, in12, in13, in14, in23, in24, in25, in26, in27, in28, in29, in30, in31, in32, in33, in34, in35, in36, in37, in38, in39, in40, in41, in42, in43, in44, in45, in46, in47, in48, in49, in50, in51, in52, in53, in54, in55, in56, in57, in58, in59, in60, in61, in62, in63, gs, en_out, en_in
  or or_1 (PCSel, BrEq, BrLt);

  // Other names for the same wires on the sheet: Opcode[6:0] = Instruction[6:0]; Ins_7_32[24:0] = Instruction[31:7];
  //   I_Imm_Funct3[2:0] = Instruction[14:12]; I_Imm_Funct7[6:0] = Instruction[31:25]

  // Notes on the sheet:
  //   INPUTS to your circuit
  //   DON'T CHANGE THE LOCATIONS OF THE INPUTS AND OUTPUTS!
  //   OUTPUT from your circuit
  //   contents of rom_1 (hex, n*v repeats v):
  //   1001 1401 1601 1081 1481 1581 1101 1201 1281 1681 1301 1381 41 41 41 1041 10c1 1141 1241 12c1 16c1
  //   1341 13c1 842 842 842 4*64 74 74 1067 17c7 2069 2041
  //   ROM FOR CONTROL LOGIC
  //   This is only if you choose to do the ROM option
  //   Reminder: If using ROM, use combinational logic for PCSel
endmodule
