// Logisim project imm-gen.circ as structural Verilog: 1 circuit, main circuit imm_gen
module imm_gen (
  input  [31:0] Instruction,
  input  [2:0] ImmSel,
  output [31:0] Immediate
);

  wire [31:0] B_Immediate, I_Immediate;

  assign I_Immediate = {{20{Instruction[31]}}, Instruction[31:20]};  // Bit_Extender bit_extender_1
  assign B_Immediate = {{19{Instruction[31]}}, {Instruction[31], Instruction[11], Instruction[30:25], Instruction[10:7], 1'b0}};  // Bit_Extender bit_extender_2
  Multiplexer #(.select(3), .width(32)) multiplexer_1 (
    .in0(I_Immediate), .in2(B_Immediate), .out(Immediate), .sel(ImmSel));  // open: in1, in3, in4, in5, in6, in7

  // Other names for the same wires on the sheet: B_1_4[3:0] = Instruction[10:7]; B_5_10[5:0] = Instruction[30:25];
  //   B_11 = Instruction[11]; B_12 = Instruction[31]

  // Notes on the sheet:
  //   INPUTS to your circuit
  //   DON'T CHANGE THE LOCATIONS OF THE INPUTS AND OUTPUTS!
  //   OUTPUT from your circuit
endmodule
